# Fritzing sketch rotary_encoder_alarm (saved by Fritzing 0.7.10b)
breadboards: 1

parts:
  Arduino2 = Arduino
  RE2 = Rotary Encoder [package=THT]
  R3 = Resistor [tolerance=±5% resistance=220 package=THT]
  R4 = Resistor [tolerance=±5% resistance=220 package=THT]
  R5 = Resistor [tolerance=±5% resistance=220 package=THT]
  Part1 = Real Time Clock Module - DS1307 RTC Breakout Board

nets:
  N1: Arduino2.D8, R5.Pin_1
  N2: Arduino2.D7, RE2.EncoderPinB, R3.Pin_0
  N3: Arduino2.D6, RE2.EncoderPinA, R4.Pin_0
  N4: Arduino2.A4, Part1.SDA
  N5: Arduino2.A5, Part1.SCL
  N6: RE2.EncoderPinC, R5.Pin_0, Part1.GND
  N7: R3.Pin_1, R4.Pin_1, Part1.5V
